# Fritzing sketch DisplayButton (saved by Fritzing 1.0.4)

parts:
  S1 = Pushbutton [package="[THT]"]
  Part1 = Arduino Uno (Rev3)
  S2 = Pushbutton [package="[THT]"]
  S3 = Pushbutton [package="[THT]"]
  S4 = Pushbutton [package="[THT]"]
  S5 = Pushbutton [package="[THT]"]  # not connected
  S6 = Pushbutton [package="[THT]"]  # not connected
  S7 = Pushbutton [package="[THT]"]  # not connected
  S8 = Pushbutton [package="[THT]"]  # not connected
  S9 = Pushbutton [package="[THT]"]  # not connected
  S10 = Pushbutton [package="[THT]"]  # not connected
  S11 = Pushbutton [package="[THT]"]  # not connected
  S12 = Pushbutton [package="[THT]"]  # not connected
  S13 = Pushbutton [package="[THT]"]  # not connected
  S14 = Pushbutton [package="[THT]"]  # not connected
  S15 = Pushbutton [package="[THT]"]  # not connected
  S16 = Pushbutton [package="[THT]"]  # not connected

nets:
  N1: S1.Pin_1, S1.Pin_2, Part1.D9_PWM
  N2: S1.Pin_3, S1.Pin_4, Part1.D8
  N3: Part1.D2, S4.Pin_3, S4.Pin_4
  N4: Part1.D3_PWM, S4.Pin_1, S4.Pin_2
  N5: Part1.D4, S3.Pin_3, S3.Pin_4
  N6: Part1.D5_PWM, S3.Pin_1, S3.Pin_2
  N7: Part1.D6_PWM, S2.Pin_3, S2.Pin_4
  N8: Part1.D7, S2.Pin_1, S2.Pin_2

notes:
  C4
  C3
  C2
  C1
  R1
  R2
  R3
  R4
