# Fritzing sketch ReactionTime (saved by Fritzing 1.0.4)
breadboards: 1

parts:
  Part1 = Arduino Uno (Rev3)
  S1 = Momentary Switch [package=ksa_sealed_tac_switch]
  S2 = Momentary Switch [package=ksa_sealed_tac_switch]
  S3 = Momentary Switch [package=ksa_sealed_tac_switch]
  R2 = Resistor [tolerance=±5% power=0.25W resistance=220 package=THT]
  R3 = Resistor [tolerance=±5% power=0.25W resistance=220 package=THT]
  R4 = Resistor [tolerance=±5% power=0.25W resistance=220 package=THT]
  LED1 = LED - 5mm [color="Orange (620nm)" current=0.030A package="5 mm [THT]"]  # not connected
  LED2 = LED - 5mm [color="Green (555nm)" current=0.030A package="5 mm [THT]"]  # not connected
  LED3 = LED - 5mm [color="Blue (470nm)" current=0.030A package="5 mm [THT]"]  # not connected

nets:
  N1: Part1.D2, R4.Pin_0
  N2: Part1.D3_PWM, R3.Pin_0
  N3: Part1.D4, R2.Pin_0
  N4: Part1.D5_PWM, S1.1
  N5: Part1.D6_PWM, S2.1
  N6: Part1.D7, S3.1
  N7: Part1.5V, S1.2, S2.2, S3.2

notes:
  R1
  R2
  R3
  C1
  C2
  C3
