# Fritzing sketch ReceiveText (saved by Fritzing 1.0.4)
breadboards: 1

parts:
  Part1 = Arduino Uno (Rev3)
  Part2 = Bluetooth HC-05 Macho
  R1 = Resistor [tolerance=±5% power=0.25W resistance=1k package=THT]
  R2 = Resistor [tolerance=±5% power=0.25W resistance=1k package=THT]
  R3 = Resistor [tolerance=±5% power=0.25W resistance=1k package=THT]

nets:
  N1: Part1.D10_PWM/SS, Part2.TXD
  N2: Part1.D11_PWM/MOSI, R1.Pin_1
  5V: Part1.5V, Part2.VCC
  GND: Part1.GND, Part2.GND, R3.Pin_0
  N3: Part2.RXD, R1.Pin_0, R2.Pin_1
  N4: R2.Pin_0, R3.Pin_1
