# Fritzing sketch PlayingMP3withButtons (saved by Fritzing 1.0.4)
breadboards: 1

parts:
  DFRobot_DFPlayer_Mini1 = DFRobot DFPlayer Mini [part_number=DFR0299]
  Part1 = Arduino Uno (Rev3)
  R1 = Resistor [tolerance=±5% power=0.25W resistance=1k package=THT]
  R2 = Resistor [tolerance=±5% power=0.25W resistance=1k package=THT]
  SP1 = SPEAKER [package=pcb_mount_speaker]
  S1 = Pushbutton [package="[THT]"]
  S2 = Pushbutton [package="[THT]"]
  S3 = Pushbutton [package="[THT]"]
  S4 = Pushbutton [package="[THT]"]
  S5 = Pushbutton [package="[THT]"]
  S6 = Pushbutton [package="[THT]"]
  S7 = Pushbutton [package="[THT]"]
  S8 = Pushbutton [package="[THT]"]
  S9 = Pushbutton [package="[THT]"]
  S10 = Pushbutton [package="[THT]"]
  S11 = Pushbutton [package="[THT]"]
  S12 = Pushbutton [package="[THT]"]
  S13 = Pushbutton [package="[THT]"]
  S14 = Pushbutton [package="[THT]"]
  S15 = Pushbutton [package="[THT]"]
  S16 = Pushbutton [package="[THT]"]

nets:
  VCC: DFRobot_DFPlayer_Mini1.VCC, Part1.5V
  N1: DFRobot_DFPlayer_Mini1.RX, R1.Pin_1
  N2: DFRobot_DFPlayer_Mini1.TX, R2.Pin_1
  N3: DFRobot_DFPlayer_Mini1.SPK_1, SP1.-
  N4: DFRobot_DFPlayer_Mini1.GND-1, DFRobot_DFPlayer_Mini1.GND-2, Part1.GND
  N5: DFRobot_DFPlayer_Mini1.SPK_2, SP1.+
  N6: Part1.D10_PWM/SS, R2.Pin_0
  N7: Part1.D11_PWM/MOSI, R1.Pin_0
  N8: S1.Pin_1, S1.Pin_2, S5.Pin_2, S9.Pin_1, S9.Pin_2, S13.Pin_1, S13.Pin_2
  N9: S1.Pin_3, S1.Pin_4, S2.Pin_3, S2.Pin_4, S3.Pin_3, S3.Pin_4, S4.Pin_3, S4.Pin_4
  N10: S2.Pin_1, S2.Pin_2, S6.Pin_2, S10.Pin_1, S10.Pin_2, S14.Pin_1, S14.Pin_2
  N11: S3.Pin_1, S3.Pin_2, S7.Pin_2, S11.Pin_1, S11.Pin_2, S15.Pin_1, S15.Pin_2
  N12: S4.Pin_1, S4.Pin_2, S8.Pin_2, S12.Pin_1, S12.Pin_2, S16.Pin_1, S16.Pin_2
  N13: S5.Pin_3, S5.Pin_4, S6.Pin_3, S6.Pin_4, S7.Pin_3, S7.Pin_4, S8.Pin_3
  N14: S9.Pin_3, S9.Pin_4, S10.Pin_3, S10.Pin_4, S11.Pin_3, S11.Pin_4, S12.Pin_3
  N15: S13.Pin_3, S13.Pin_4, S14.Pin_3, S14.Pin_4, S15.Pin_3, S15.Pin_4, S16.Pin_3

notes:
  +
  –
  S1
  S2
  S3
  S4
  S5
  S6
  S7
  S8
  S9
  S10
  S11
  S12
  S13
  S14
  S15
  S16
  C4
  C3
  C2
  C1
  R1
  R2
  R3
  R4
