# Fritzing sketch MultiplexingDisplays (saved by Fritzing 1.0.4)
breadboards: 1

parts:
  7_Segment1 = 7 Segment Display
  R1 = Resistor [tolerance=±5% power=0.25W resistance=220 package=THT]
  Part1 = Arduino Uno (Rev3)
  7_Segment2 = 7 Segment Display
  R2 = Resistor [tolerance=±5% power=0.25W resistance=220 package=THT]

nets:
  N1: 7_Segment1.Segment_E, Part1.D9_PWM, 7_Segment2.Segment_E
  N2: 7_Segment1.Segment_D, Part1.D8, 7_Segment2.Segment_D
  N3: 7_Segment1.common_cathode, R1.Pin_1
  N4: 7_Segment1.Segment_C, Part1.D7, 7_Segment2.Segment_C
  N5: 7_Segment1.Segment_DP, Part1.D6_PWM, 7_Segment2.Segment_DP
  N6: 7_Segment1.Segment_B, Part1.D5_PWM, 7_Segment2.Segment_B
  N7: 7_Segment1.Segment_A, Part1.D4, 7_Segment2.Segment_A
  N8: 7_Segment1.Segment_F, Part1.D3_PWM, 7_Segment2.Segment_F
  N9: 7_Segment1.Segment_G, Part1.D2, 7_Segment2.Segment_G
  N10: R1.Pin_0, Part1.D13/SCK
  N11: Part1.D12/MISO, R2.Pin_0
  N12: 7_Segment2.common_cathode, R2.Pin_1
