# Fritzing sketch ScrollingText (saved by Fritzing 1.0.4)
breadboards: 1

parts:
  Part1 = Arduino Uno (Rev3)
  Grove1 = Grove 4 Digit Display

nets:
  N1: Part1.A4/SDA, Grove1.CLK
  N2: Part1.A5/SCL, Grove1.DIO
  5V: Part1.5V, Grove1.VCC
  GND: Part1.GND, Grove1.GND

notes:
  SCL
  SDA
  VCC un
  uI2C
  GND
