# Fritzing sketch CharlieplexingLEDs (saved by Fritzing 1.0.4)
breadboards: 1

parts:
  Mod1 = Amica NodeMCU DEVKIT 1.0
  LED1 = LED - 5mm [color="Red (633nm)" current=0.030A package="5 mm [THT]"]
  R1 = Resistor [tolerance=±5% power=0.25W resistance=220 package=THT]
  LED2 = LED - 5mm [color="Red (633nm)" current=0.030A package="5 mm [THT]"]
  R2 = Resistor [tolerance=±5% power=0.25W resistance=220 package=THT]
  LED3 = LED - 5mm [color="Orange (620nm)" current=0.030A package="5 mm [THT]"]
  R3 = Resistor [tolerance=±5% power=0.25W resistance=220 package=THT]
  LED4 = LED - 5mm [color="Orange (620nm)" current=0.030A package="5 mm [THT]"]
  R4 = Resistor [tolerance=±5% power=0.25W resistance=220 package=THT]
  LED5 = LED - 5mm [color="Green (555nm)" current=0.030A package="5 mm [THT]"]
  LED6 = LED - 5mm [color="Green (555nm)" current=0.030A package="5 mm [THT]"]
  R5 = Resistor [tolerance=±5% power=0.25W resistance=220 package=THT]
  R6 = Resistor [tolerance=±5% power=0.25W resistance=220 package=THT]

nets:
  N1: Mod1.pin5, R3.Pin_1, LED4.anode, LED6.anode, R5.Pin_1
  N2: Mod1.pin6, R1.Pin_1, LED2.anode, LED5.anode, R6.Pin_0
  N3: Mod1.pin8, LED1.anode, R2.Pin_0, LED3.anode, R4.Pin_0
  N4: LED1.cathode, R1.Pin_0
  N5: LED2.cathode, R2.Pin_1
  N6: LED3.cathode, R3.Pin_0
  N7: LED4.cathode, R4.Pin_1
  N8: LED5.cathode, R5.Pin_0
  N9: LED6.cathode, R6.Pin_1

notes:
  18
  17
  16
