# Fritzing sketch FrequencyGoertzel (saved by Fritzing 1.0.4)
breadboards: 1

parts:
  Part1 = Arduino Uno (Rev3)
  Part3 = Breakout Board for Electret Microphone  # not connected
  Part4 = TRRS 3.5mm Jack Breakout

nets:
  N1: Part1.A0, Part4.TIP
  N2: Part1.5V, Part4.RING2
  N3: Part1.GND, Part4.SLEEVE, Part4.RING1

notes:
  GND
  Vdd
  Gain
  Out
  Mikrofona kontaktu AR nepieslēdz
