# Fritzing sketch VariousSounds (saved by Fritzing 1.0.4)
breadboards: 1

parts:
  Part1 = Arduino Uno (Rev3)
  Mod1 = Passive Buzzer
  S1 = Pushbutton [package="[SMD]"]
  S2 = Pushbutton [package="[SMD]"]
  S3 = Pushbutton [package="[SMD]"]

nets:
  N1: Part1.D8, Mod1.NC
  N2: Part1.D5_PWM, S1.Pin_2
  N3: Part1.D6_PWM, S2.Pin_2
  N4: Part1.D7, S3.Pin_2
  N5: Part1.5V, Mod1.S
  N6: Part1.GND, Mod1.-, S1.Pin_3, S1.Pin_4, S2.Pin_3, S2.Pin_4, S3.Pin_3, S3.Pin_4

notes:
  VCC
  GND
  I/O
  C1
  C2
  C3
  R1
  R2
  R3
