# Fritzing sketch LED_and_Resistor (saved by Fritzing 1.0.4)
breadboards: 1

parts:
  Part1 = Arduino Uno (Rev3)
  LED1 = LED - 5mm [color="Red (633nm)" current=0.030A package="5 mm [THT]"]
  R1 = Resistor [tolerance=±5% power=0.25W resistance=220 package=THT]

nets:
  N1: Part1.GND, R1.Pin_0
  N2: Part1.5V, LED1.anode
  N3: LED1.cathode, R1.Pin_1
