# Fritzing sketch Potentiometer_multiple_LED (saved by Fritzing 1.0.4)
breadboards: 1

parts:
  R1 = Slide Potentiometer [maximum_resistance=10kΩ knob_status=50% power=0.5W package=THT]
  R2 = Resistor [tolerance=±5% power=0.25W resistance=220 package=THT]
  Part1 = Arduino Uno (Rev3)
  LED1 = LED - 5mm [color="Red (633nm)" current=0.030A package="5 mm [THT]"]
  LED2 = LED - 5mm [color="Orange (612nm)" current=0.030A package="5 mm [THT]"]
  LED3 = LED - 5mm [color="Yellow (592nm)" current=0.030A package="5 mm [THT]"]
  LED4 = LED - 5mm [color="Green (565nm)" current=0.030A package="5 mm [THT]"]

nets:
  N1: R1.leg1, Part1.5V
  N2: R1.wiper, R2.Pin_0
  N3: R1.leg2, Part1.GND, LED1.cathode, LED2.cathode, LED3.cathode, LED4.cathode
  N4: R2.Pin_1, LED1.anode, LED2.anode, LED3.anode, LED4.anode

notes:
  OTA
  VCC
  GND
