# Fritzing sketch EnablingBlinker (saved by Fritzing 1.0.4)
breadboards: 1

parts:
  R1 = Slide Potentiometer [maximum_resistance=10kΩ knob_status=50% power=0.5W package=THT]
  R2 = Resistor [tolerance=±5% power=0.25W resistance=220 package=THT]
  LED1 = LED - 5mm [color="Red (633nm)" current=0.030A package="5 mm [THT]"]
  Part1 = Arduino Uno (Rev3)

nets:
  N1: R1.leg1, Part1.5V
  N2: R1.wiper, Part1.A0
  N3: R1.leg2, R2.Pin_0, Part1.GND
  N4: R2.Pin_1, LED1.cathode
  N5: LED1.anode, Part1.D13/SCK

notes:
  OTA
  VCC
  GND
