# Fritzing sketch PWMwithGammaCorrection (saved by Fritzing 1.0.4)
breadboards: 1

parts:
  R1 = Resistor [tolerance=±5% power=0.25W resistance=220 package=THT]
  LED1 = LED - 5mm [color="Red (633nm)" current=0.030A package="5 mm [THT]"]
  Part1 = Arduino Uno (Rev3)
  R2 = Slide Potentiometer [maximum_resistance=10kΩ knob_status=50% power=0.5W package=THT]

nets:
  N1: R1.Pin_0, Part1.D9_PWM
  N2: R1.Pin_1, LED1.anode
  N3: LED1.cathode, Part1.GND, R2.leg2
  N4: Part1.A0, R2.wiper
  N5: Part1.5V, R2.leg1

notes:
  OTA
  VCC
  GND
