# Fritzing sketch BlinkingWithRelay (saved by Fritzing 1.0.4)
breadboards: 2

parts:
  WeMos_D1_Mini_Relay_Shield_V1 = WeMos D1 Mini Relay Shield V2
  Part1 = Arduino Uno (Rev3)
  Part2 = Arduino Uno (Rev3)
  LED1 = LED - 5mm [color="Orange (620nm)" current=0.030A package="5 mm [THT]"]
  R1 = Resistor [tolerance=±5% power=0.25W resistance=220 package=THT]
  LED2 = LED - 5mm [color="Blue (470nm)" current=0.030A package="5 mm [THT]"]
  R2 = Resistor [tolerance=±5% power=0.25W resistance=220 package=THT]

nets:
  N1: WeMos_D1_Mini_Relay_Shield_V1.COM, Part2.5V
  GND: WeMos_D1_Mini_Relay_Shield_V1.GND, Part1.GND
  VCC: WeMos_D1_Mini_Relay_Shield_V1.VCC, Part1.5V
  N2: WeMos_D1_Mini_Relay_Shield_V1.NC, LED2.anode
  N3: WeMos_D1_Mini_Relay_Shield_V1.NO, LED1.anode
  N4: Part2.GND, R1.Pin_0, R2.Pin_0
  N5: LED1.cathode, R1.Pin_1
  N6: LED2.cathode, R2.Pin_1

notes:
  NC
  NO
  COM
  Lietotāju ķēde
  Vadības ķēde

custom parts:
  WeMos D1 Mini Relay Shield V2: An updated relay shield.
