# Fritzing sketch MorseSignals (saved by Fritzing 1.0.4)
breadboards: 1

parts:
  WeMos_D1_Mini_Relay_Shield_V1 = WeMos D1 Mini Relay Shield V2
  Part1 = Arduino Uno (Rev3)
  HC-SR04_Sensor_1 = HC-SR04 Ultrasonic Distance Sensor  # not connected

nets:
  GND: WeMos_D1_Mini_Relay_Shield_V1.GND, Part1.GND
  VCC: WeMos_D1_Mini_Relay_Shield_V1.VCC, Part1.5V

custom parts:
  WeMos D1 Mini Relay Shield V2: An updated relay shield.
