# Fritzing sketch PositionSequence (saved by Fritzing 1.0.4)
breadboards: 1

parts:
  Part1 = Arduino Uno (Rev3)
  M2 = Dagu DGServo 9g (Pan and tilt) [part_number=RS001B]
  R1 = Resistor [tolerance=±5% power=0.25W resistance=220 package=THT]
  LED1 = LED - 5mm [color="Red (633nm)" current=0.030A package="5 mm [THT]"]
  LED2 = LED - 5mm [color="Green (555nm)" current=0.030A package="5 mm [THT]"]
  LED3 = LED - 5mm [color="Blue (470nm)" current=0.030A package="5 mm [THT]"]
  R2 = Resistor [tolerance=±5% power=0.25W resistance=220 package=THT]

nets (from the schematic view):
  N1: Part1.D9_PWM, M2.pulse
  N2: Part1.D10_PWM/SS, LED1.anode
  N3: Part1.D11_PWM/MOSI, LED2.anode
  N4: Part1.D12/MISO, LED3.anode
  GND: Part1.GND, M2.gnd, R1.Pin_0, R2.Pin_0
  5V: Part1.5V, M2.vcc
  N5: R1.Pin_1, LED1.cathode, LED2.cathode
  N6: LED3.cathode, R2.Pin_1
