# Fritzing sketch TurnForthAndBack (saved by Fritzing 1.0.4)

parts:
  Part1 = Arduino Uno (Rev3)
  M1 = Dagu DGServo 9g (Top view) [part_number=RS001B]

nets:
  N1: Part1.D9_PWM, M1.pulse
  GND: Part1.GND, M1.gnd
  5V: Part1.5V, M1.vcc

notes:
  5V
