# Fritzing sketch TurningByPotentiometer (saved by Fritzing 1.0.4)
breadboards: 1

parts:
  Part1 = Arduino Uno (Rev3)
  R1 = Resistor [tolerance=±5% power=0.25W resistance=220 package=THT]
  LED1 = LED - 5mm [color="Red (633nm)" current=0.030A package="5 mm [THT]"]
  LED2 = LED - 5mm [color="Green (555nm)" current=0.030A package="5 mm [THT]"]
  R2 = Slide Potentiometer [maximum_resistance=10kΩ knob_status=50% power=0.5W package=THT]
  M2 = Dagu DGServo 9g (Pan and tilt) [part_number=RS001B]

nets:
  N1: Part1.A0, R2.wiper, R2.wiper-1
  N2: Part1.D9_PWM, M2.pulse
  N3: Part1.D10_PWM/SS, LED1.anode
  N4: Part1.D11_PWM/MOSI, LED2.anode
  GND: Part1.GND, R1.Pin_0, R2.leg1, M2.gnd
  5V: Part1.5V, R2.leg2, M2.vcc
  N5: R1.Pin_1, LED1.cathode, LED2.cathode

notes:
  OTA
  VCC
  GND
