# Fritzing sketch BranchingOut (saved by Fritzing 1.0.4)
breadboards: 1

parts:
  Q1 = TRANSISTOR_NPN [package=to-92-ammo]
  R1 = Resistor [tolerance=±5% power=0.25W resistance=220 package=THT]
  S1 = Pushbutton [package="[THT]"]  # not connected
  LED1 = LED - 5mm [color="Red (633nm)" current=0.030A package="5 mm [THT]"]
  R2 = Resistor [tolerance=±5% power=0.25W resistance=220 package=THT]
  LED2 = LED - 5mm [color="Orange (620nm)" current=0.030A package="5 mm [THT]"]
  R3 = Resistor [tolerance=±5% power=0.25W resistance=220 package=THT]
  LED3 = LED - 5mm [color="Green (555nm)" current=0.030A package="5 mm [THT]"]
  R4 = Resistor [tolerance=±5% power=0.25W resistance=220 package=THT]
  LED4 = LED - 5mm [color="Blue (470nm)" current=0.030A package="5 mm [THT]"]
  R5 = Resistor [tolerance=±5% power=0.25W resistance=220 package=THT]
  S2 = Pushbutton [package="[THT]"]  # not connected
  Q2 = TRANSISTOR_NPN [package=to-92-ammo]
  Q3 = TRANSISTOR_NPN [package=to-92-ammo]
  R6 = Resistor [tolerance=±5% power=0.25W resistance=220 package=THT]
  R7 = Resistor [tolerance=±5% power=0.25W resistance=220 package=THT]
  Part1 = Arduino Uno (Rev3)

nets:
  N1: Q1.B, R1.Pin_0
  N2: LED1.cathode, R2.Pin_1
  N3: R2.Pin_0, R3.Pin_0, R4.Pin_0, R5.Pin_0, Part1.GND
  N4: LED2.cathode, R3.Pin_1
  N5: LED3.cathode, R4.Pin_1
  N6: LED4.cathode, R5.Pin_1
  N7: Q2.B, R6.Pin_0
  N8: Q3.B, R7.Pin_0

notes:
  R1
  C1
  R2
  C2
  No Arduino tikai GND un 5V kontakti
