# Fritzing sketch NandGate (saved by Fritzing 1.0.4)
breadboards: 1

parts:
  Part1 = Arduino Uno (Rev3)
  S1 = Pushbutton [package="[THT]"]
  R2 = Resistor [tolerance=±5% power=0.25W resistance=10k package=THT]
  LED1 = LED - 5mm [color="Yellow (585nm)" current=0.030A package="5 mm [THT]"]
  R3 = Resistor [tolerance=±5% power=0.25W resistance=220 package=THT]
  R4 = Resistor [tolerance=±5% power=0.25W resistance=10k package=THT]
  R5 = Resistor [tolerance=±5% power=0.25W resistance=220 package=THT]
  S2 = Pushbutton [package="[THT]"]
  LED2 = LED - 5mm [color="Yellow (585nm)" current=0.030A package="5 mm [THT]"]
  R6 = Resistor [tolerance=±5% power=0.25W resistance=1k package=THT]
  R7 = Resistor [tolerance=±5% power=0.25W resistance=1k package=THT]
  Q1 = NPN-Transistor [package="TO92 [THT]"]
  Q2 = NPN-Transistor [package="TO92 [THT]"]
  LED3 = LED - 5mm [color="Blue (470nm)" current=0.030A package="5 mm [THT]"]  # not connected
  R8 = Resistor [tolerance=±5% power=0.25W resistance=1k package=THT]
  R9 = Resistor [tolerance=±5% power=0.25W resistance=220 package=THT]

nets:
  N1: Part1.5V, S1.Pin_1, S2.Pin_1, S2.Pin_2, R8.Pin_1
  N2: Part1.GND, R2.Pin_0, R3.Pin_0, R4.Pin_0, R5.Pin_0, Q1.E, R9.Pin_1
  N3: S1.Pin_3, LED1.anode, R4.Pin_1, R6.Pin_0
  N4: R2.Pin_1, S2.Pin_3, LED2.anode, R7.Pin_0
  N5: LED1.cathode, R3.Pin_1
  N6: R5.Pin_1, LED2.cathode
  N7: R6.Pin_1, Q1.C
  N8: R7.Pin_1, Q2.C
  N9: Q1.B, Q2.E
  N10: Q2.B, R8.Pin_0
