# Fritzing sketch NotGate (saved by Fritzing 1.0.4)
breadboards: 1

parts:
  LED1 = LED - 5mm [color="Blue (470nm)" current=0.030A package="5 mm [THT]"]
  R1 = Resistor [tolerance=±5% power=0.25W resistance=220 package=THT]
  Q1 = NPN-Transistor [package="TO92 [THT]"]
  R2 = Resistor [tolerance=±5% power=0.25W resistance=1k package=THT]
  Part1 = Arduino Uno (Rev3)
  R3 = Resistor [tolerance=±5% power=0.25W resistance=10k package=THT]
  U1 = SWITCH_SPDT [package=kps-1290]
  S1 = Pushbutton [package="[THT]"]

nets:
  N1: LED1.cathode, Q1.C, Part1.GND, R3.Pin_0, U1.S, S1.Pin_1, S1.Pin_2
  N2: LED1.anode, R1.Pin_1
  N3: R1.Pin_0, Q1.E, R2.Pin_1
  N4: Q1.B, R3.Pin_1
  N5: R2.Pin_0, Part1.5V, U1.O, S1.Pin_3, S1.Pin_4
