# Fritzing sketch NotGateButton (saved by Fritzing 1.0.4)
breadboards: 1

parts:
  Part1 = Arduino Uno (Rev3)
  R1 = Resistor [tolerance=±5% power=0.25W resistance=220 package=THT]
  S1 = Pushbutton [package="[THT]"]
  LED1 = LED - 5mm [color="Red (633nm)" current=0.030A package="5 mm [THT]"]

nets:
  N1: Part1.GND, R1.Pin_1, S1.Pin_1, S1.Pin_2, S1.Pin_4, LED1.cathode, LED1.anode
  N2: Part1.5V, R1.Pin_0
