# Fritzing sketch OrGate (saved by Fritzing 1.0.4)
breadboards: 1

parts:
  Part1 = Arduino Uno (Rev3)
  S1 = Momentary Switch [package=ksa_sealed_tac_switch]
  S2 = Momentary Switch [package=ksa_sealed_tac_switch]
  R1 = Resistor [tolerance=±5% power=0.25W resistance=10k package=THT]
  R2 = Resistor [tolerance=±5% power=0.25W resistance=10k package=THT]
  U1 = TRANSISTOR_NPN_2 [package=to-92]
  U2 = TRANSISTOR_NPN_2 [package=to-92]
  LED1 = LED - 5mm [color="Red (633nm)" current=0.030A package="5 mm [THT]"]
  R3 = Resistor [tolerance=±5% power=0.25W resistance=220 package=THT]
  R4 = Resistor [tolerance=±5% power=0.25W resistance=1k package=THT]

nets (from the schematic view):
  N1: Part1.5V, S1.2, S2.2, U1.C, U2.C
  N2: Part1.GND, LED1.cathode, R4.Pin_0
  N3: S1.3, R1.Pin_0
  N4: S2.3, R2.Pin_0
  N5: R1.Pin_1, U1.B
  N6: R2.Pin_1, U2.B
  N7: U1.E, U2.E
  N8: LED1.anode, R3.Pin_1
  N9: R3.Pin_0, R4.Pin_1

notes:
  R1
  C1
  C2
  Col1
  Col2
  Row1
  Collector
  Base
  Emitter
