# Fritzing sketch DistanceToSerial (saved by Fritzing 1.0.4)
breadboards: 1

parts:
  Part1 = Arduino Uno (Rev3)
  HC-SR04_Sensor_1 = HC-SR04 Ultrasonic Distance Sensor

nets:
  N1: Part1.D9_PWM, HC-SR04_Sensor_1.TRIG
  N2: Part1.D10_PWM/SS, HC-SR04_Sensor_1.ECHO
  5V: Part1.5V, HC-SR04_Sensor_1.VCC
  GND: Part1.GND, HC-SR04_Sensor_1.GND
