# Fritzing sketch led-and-resistor (saved by Fritzing 1.0.4)
breadboards: 1

parts:
  R1 = Resistor [tolerance=±5% power=0.25W resistance=220 package=THT]
  LED = LED - 5mm [color="Red (633nm)" current=0.030A package="5 mm [THT]"]
  5V = 4 x AAA Battery Mount [internal_resistance=5Ω]

nets:
  N1: R1.Pin_0, 5V.+
  N2: R1.Pin_1, LED.anode
  N3: LED.cathode, 5V.-
