# Fritzing sketch potentiometer (saved by Fritzing 1.0.4)

parts:
  R1 = Slide Potentiometer [maximum_resistance=10kΩ knob_status=50% power=0.5W package=THT]
  Part1 = Arduino Uno (Rev3)

nets:
  N1: R1.leg1, Part1.GND
  N2: R1.wiper, R1.wiper-1, Part1.A0
  N3: R1.leg2, Part1.5V

notes:
  OTA
  GND
  VCC
