# Fritzing sketch button-pad (saved by Fritzing 1.0.4)
breadboards: 1

parts:
  S1 = SWITCH-MOMENTARY-2 [package=tactile-switch-1101ne]
  S2 = SWITCH-MOMENTARY-2 [package=tactile-switch-1101ne]
  LED1 = LED - 5mm [color="Blue (470nm)" current=0.030A package="5 mm [THT]"]  # not connected
  R1 = Resistor [tolerance=±5% power=0.25W resistance=220 package=THT]
  LED2 = LED - 5mm [color="Green (565nm)" current=0.030A package="5 mm [THT]"]  # not connected
  R2 = Resistor [tolerance=±5% power=0.25W resistance=220 package=THT]
  Part1 = Arduino Uno (Rev3)

nets:
  N1: S1.2, S2.2, Part1.GND
  N2: R1.Pin_0, R2.Pin_0, Part1.5V
