# Fritzing sketch with-relay-jqc-3f (saved by Fritzing 1.0.4)
breadboards: 1

parts:
  LED1 = LED - 5mm [color="Blue (470nm)" current=0.030A package="5 mm [THT]"]  # not connected
  R1 = Resistor [tolerance=±5% power=0.25W resistance=220 package=THT]
  Part1 = Arduino Uno (Rev3)
  WeMos_D1_Mini_Relay_Shield_V2 = WeMos D1 Mini Relay Shield V2
  LED2 = LED - 5mm [color="Red (633nm)" current=0.030A package="5 mm [THT]"]
  R2 = Resistor [tolerance=±5% power=0.25W resistance=220 package=THT]

nets:
  N1: R1.Pin_0, Part1.D13/SCK
  5V: Part1.5V, WeMos_D1_Mini_Relay_Shield_V2.COM, WeMos_D1_Mini_Relay_Shield_V2.VCC
  GND: Part1.GND, WeMos_D1_Mini_Relay_Shield_V2.GND, LED2.cathode
  N2: WeMos_D1_Mini_Relay_Shield_V2.NO, R2.Pin_1
  N3: LED2.anode, R2.Pin_0

custom parts:
  WeMos D1 Mini Relay Shield V2: An updated relay shield.
